# Fritzing sketch Schematic_Silva (saved by Fritzing 1.0.4)
breadboards: 1

parts:
  A1 = Particle - Photon2
  Part1 = Adafruit LC709203F Fuel Gauge and Battery Monitor [part_number="Adafruit #4712"]
  Part2 = Adafruit USB LiIon/LiPoly Charger [part_number="Adafruit #259"]
  M1 = DC Motor [voltage_(max)=6V voltage_(min)=3V]
  M2 = DC Motor [voltage_(max)=6V voltage_(min)=3V]
  U1 = LIPO-2000mAh [package=lipo-2000]
  U2 = SWITCH_SPDT [package=kps-1290]

nets:
  N1: A1.Pin_2, Part1.VCC
  GND: A1.Pin_4, A1.Pin_30, Part1.GND, Part2.GND, M2.pin_2, U1.-, U2.S
  N2: A1.Pin_17, Part1.SDA
  N3: A1.Pin_18, Part1.SCL
  N4: A1.Pin_27, U2.P
  N5: A1.Pin_28, Part1.VBAT, Part2.BATT, U1.+
  N6: Part2.5.0V, M1.pin_1
  N7: M1.pin_2, M2.pin_1

custom parts:
  Particle - Photon2: The Photon 2 is a microcontroller and Wi-Fi networking developed by particle. Features: 802.11a/b/g/n Wi-Fi, 2.4 GHz and 5 GHz Integrated PCB antenna Integrated U.FL connector for external antenna Integrated RF switch BLE 5 using same antenna as Wi-Fi Realtek RTL8721DM MCU ARM Cortex M33 CPU, 200 MHz 2048 KB (2 MB) user application maximum size 3072 KB (3 MB) of RAM available to user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
  Adafruit LC709203F Fuel Gauge and Battery Monitor: Low cost Lithium Polymer batteries have revolutionized electronics - they're thin, they're light, they can be regulated down to 3.3V and they're easy to charge. On your phone, there's a little image of a battery cell that tells you the percentage of charge - so you know when you absolutely need to plug it in and when you can stay untethered. The Adafruit LC709203F LiPoly / LiIon Fuel Gauge and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
  Adafruit USB LiIon/LiPoly Charger: This is a Lithium Ion and Lithium Polymer battery charger based on the MCP73833. It uses a USB mini-B for connection to any computer or 'USB wall adapter'. Charging is performed in three stages: first a preconditioning charge, then a constant-current fast charge and finally a constant-voltage trickle charge to keep the battery topped-up. The fast-charge current is 500mA by default, but is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
